// Logisim project part1.circ as structural Verilog: 1 circuit, main circuit main
module main (
  input  s,
  input  x,
  input  y,
  output f,
  output out_5
);

  wire n7404_1_p2, n7404_2_p8, n7408_1_p3, n7408_1_p6, n7408_2_p3, n7408_2_p4, n7408_2_p6, n7408_2_p9,
       n7408_2_p10, n7408_2_p11, n7408_2_p12, n7432_1_p3;

  // _7404 7404_1: pin names not known; wires that end beside it: s, n7404_1_p2
  // _7408 7408_1: pin names not known; wires that end beside it: n7404_1_p2, x, n7408_1_p3, s, y, n7408_1_p6
  // _7432 7432_1: pin names not known; wires that end beside it: n7408_1_p3, n7408_1_p6, n7432_1_p3
  // _7408 7408_2: pin names not known; wires that end beside it: s, s, n7408_2_p3, n7408_2_p4, x, n7408_2_p6, s, y, n7408_2_p9, n7408_2_p10, n7408_2_p11, n7408_2_p12
  // _7404 7404_2: pin names not known; wires that end beside it: n7408_2_p3, n7408_2_p4, n7408_2_p6, n7408_2_p11, n7408_2_p9, n7408_2_p10, n7408_2_p12, n7404_2_p8
endmodule
