// Logisim project part2.circ as structural Verilog: 1 circuit, main circuit main
module main (
  input  a,
  input  c,
  input  b,
  input  d,
  output f
);

  wire n7404_1_p2, n7404_1_p4, n7408_1_p1, n7408_1_p4, n7432_1_p1;

  // _7404 7404_1: pin names not known; wires that end beside it: a, n7404_1_p2, c, n7404_1_p4, b
  // _7408 7408_1: pin names not known; wires that end beside it: n7408_1_p1, n7404_1_p2, n7404_1_p4, n7408_1_p4, n7408_1_p1, d
  // _7432 7432_1: pin names not known; wires that end beside it: n7432_1_p1, n7408_1_p4, n7432_1_p1, f
endmodule
